# Fritzing sketch Arduino_Wiring (saved by Fritzing 1.0.4)
breadboards: 1

parts:
  LCD2004-I2C1 = LCD2004-I2C
  Bauteil1 = Arduino Ethernet Shield (Rev3)
  R1 = Rotary Potentiometer (Small) [maximum_resistance=10kΩ knob_status=50% power=0.5W package=THT]

nets:
  GND: LCD2004-I2C1.GND, Bauteil1.GND, R1.leg2
  VCC: LCD2004-I2C1.VCC, Bauteil1.5V, R1.leg1
  N1: LCD2004-I2C1.SDA, Bauteil1.A4/SDA
  N2: LCD2004-I2C1.SCL, Bauteil1.A5/SCL
  N3: Bauteil1.A0, R1.wiper

custom parts:
  LCD2004-I2C: A standard character display with 4x20 characters. Comes in many colors with LCM2004 IIC attached.
