# Fritzing sketch D1_Mini_Wiring (saved by Fritzing 1.0.4)
breadboards: 1

parts:
  WeMos_D1_Mini1 = WeMos D1 Mini
  Bauteil1 = BME280

nets:
  3V3: WeMos_D1_Mini1.3V3, Bauteil1.VIN
  N1: WeMos_D1_Mini1.D1, Bauteil1.SCL
  N2: WeMos_D1_Mini1.D2, Bauteil1.SDA
  N3: WeMos_D1_Mini1.G, Bauteil1.GND
