# Fritzing sketch ESP32_Wiring (saved by Fritzing 1.0.4)
breadboards: 1

parts:
  U1 = ESP32-38PinWide [part_number=ESP32-38PinWide]
  R1 = Resistor [tolerance=±5% power=0.25W resistance=220 package=THT]
  LED1 = LED - 5mm [color="Red (633nm)" current=0.030A package="5 mm [THT]"]
  S1 = Pushbutton [package="[THT]"]

nets:
  N1: U1.GPIO5, LED1.anode
  N2: U1.GND, R1.Pin_1, S1.Pin_3, S1.Pin_4
  N3: U1.GPIO21, S1.Pin_1, S1.Pin_2
  N4: R1.Pin_0, LED1.cathode

custom parts:
  ESP32-38PinWide: Generic 38-Pin ESP32 with wide format (only access to one side of pins on a breadboard) based on Stephen Lilley's HiLetgo ESP-WROOM-32 ESP32 ESP-32S Development Board.
